# Fritzing sketch condicionamento_pcb(copy) (saved by Fritzing 0.9.3b)
circuit board: 5cm x 5cm
breadboards: 1

parts:
  LM1 = LM741 [part_number=LM741 package="DIP (Dual Inline) [THT]"]
  C1 = Electrolytic Capacitor [capacitance=10µF package="100 mil [THT, electrolytic]"]
  R1 = Resistor [tolerance=±5% resistance=220 package=THT]
  R2 = Resistor [tolerance=±5% resistance=220 package=THT]
  R3 = Resistor [tolerance=±5% resistance=220 package=THT]
  R4 = Resistor [tolerance=±5% resistance=220 package=THT]
  D1 = Rectifier Diode [part_number=1N4001 package="300 mil [THT]"]
  D2 = Rectifier Diode [part_number=1N4001 package="300 mil [THT]"]
  U1 = Voltage Regulator - 5V [package="TO220 [THT]"]
  C3 = Ceramic Capacitor [capacitance=100nF package="200 mil [THT, multilayer]"]
  C2 = Ceramic Capacitor [capacitance=100nF package="200 mil [THT, multilayer]"]
  C4 = Ceramic Capacitor [capacitance=100nF package="200 mil [THT, multilayer]"]
  C+12 = Ceramic Capacitor [capacitance=100nF package="200 mil [THT, multilayer]"]
  C+5 = Ceramic Capacitor [capacitance=100nF package="200 mil [THT, multilayer]"]
  signal_In = screw terminal, 2 pins
  power_12V = screw terminal, 3 pins
  signal_Out = screw terminal, 2 pins

nets:
  N1: LM1.pin2, LM1.pin6, C1.+
  N2: LM1.pin3, signal_In.pin2
  N3: LM1.pin4, C3.1, power_12V.pin3
  N4: LM1.pin7, U1.input_voltage, C2.1, C+12.1, power_12V.pin1
  N5: C1.-, R1.Pin_0, R2.Pin_1, R3.Pin_0
  N6: R1.Pin_1, D1.cathode, U1.output_voltage, C+5.0
  GND: R2.Pin_0, D2.anode, U1.GND, C3.0, C2.0, C4.0, C+12.0, C+5.1, signal_In.pin1, power_12V.pin2, signal_Out.pin2
  N7: R3.Pin_1, R4.Pin_0, D1.anode, D2.cathode
  N8: R4.Pin_1, C4.1, signal_Out.pin1

notes:
  cond
  condicionamento

custom parts:
  LM741: This is a single Op Amp DIP.
