# Fritzing sketch condicionamento_pcb_baseado_ad826 (saved by Fritzing 0.9.3b)
circuit board: 8cm x 5cm
breadboards: 1

parts:
  AD826 = TL072 [package="DIP (Dual Inline) [THT]"]
  Componente1 = TL072 [package="DIP (Dual Inline) [THT]"]
  AD826_1 = TL072 [package="DIP (Dual Inline) [THT]"]
  AD826_2 = TL072 [package="DIP (Dual Inline) [THT]"]
  alimentacao_-V_GND_+V = female pin header, 3 pins [form="♀ (female)"]
  C1 = Ceramic Capacitor [capacitance=100nF package="100 mil [THT, multilayer]"]
  C2 = Ceramic Capacitor [capacitance=100nF package="100 mil [THT, multilayer]"]
  SignOutEletrodo_SignOutSentinela = female pin header, 2 pins [form="♀ (female)"]
  GND_Offset = female pin header, 2 pins [form="♀ (female)"]
  SignInEletrodo_SignInSentinela = female pin header, 2 pins [form="♀ (female)"]
  C3 = Electrolytic Capacitor [capacitance=10µF voltage=16V package="100 mil [THT, electrolytic]"]
  C4 = Electrolytic Capacitor [capacitance=10µF voltage=16V package="100 mil [THT, electrolytic]"]
  R1 = Resistor [tolerance=±5% resistance=100 package=THT]
  R2 = Resistor [tolerance=±5% resistance=220 package=THT]
  R3 = Resistor [tolerance=±5% resistance=10k package=THT]
  R4 = Resistor [tolerance=±5% resistance=10k package=THT]
  D1 = Rectifier Diode [part_number=1N4001 package="300 mil [THT]"]
  D2 = Rectifier Diode [part_number=1N4001 package="300 mil [THT]"]
  C5 = Ceramic Capacitor [capacitance=0.22mF package="100 mil [THT, multilayer]"]
  R5 = Resistor [tolerance=±5% resistance=100 package=THT]
  R6 = Resistor [tolerance=±5% resistance=220 package=THT]
  R7 = Resistor [tolerance=±5% resistance=10k package=THT]
  R8 = Resistor [tolerance=±5% resistance=10k package=THT]
  D3 = Rectifier Diode [part_number=1N4001 package="300 mil [THT]"]
  D4 = Rectifier Diode [part_number=1N4001 package="300 mil [THT]"]
  C6 = Ceramic Capacitor [capacitance=0.22mF package="100 mil [THT, multilayer]"]

nets:
  N1: AD826.connector0, AD826.connector1, AD826_1.pin1, AD826_1.pin2, C3.+
  N2: AD826.connector2, AD826_1.pin3, SignInEletrodo_SignInSentinela.pin2
  N3: AD826.connector3, Componente1.pin4, alimentacao_-V_GND_+V.pin3, C1.1
  N4: AD826.connector4, AD826_2.pin5, SignInEletrodo_SignInSentinela.pin1
  N5: AD826.connector5, AD826.connector6, AD826_2.pin6, AD826_2.pin7, C4.+
  N6: AD826.connector7, Componente1.pin8, alimentacao_-V_GND_+V.pin1, C2.1
  GND: alimentacao_-V_GND_+V.pin2, C1.0, C2.0, GND_Offset.pin1, R3.Pin_0, D1.anode, C5.0, R7.Pin_0, D3.anode, C6.0
  N7: SignOutEletrodo_SignOutSentinela.pin1, R2.Pin_1, C5.1
  N8: SignOutEletrodo_SignOutSentinela.pin2, R6.Pin_1, C6.1
  N9: GND_Offset.pin2, R4.Pin_1, D2.cathode, R8.Pin_1, D4.cathode
  N10: C3.-, R1.Pin_0, R3.Pin_1, R4.Pin_0
  N11: C4.-, R5.Pin_0, R7.Pin_1, R8.Pin_0
  N12: R1.Pin_1, R2.Pin_0, D1.cathode, D2.anode
  N13: R5.Pin_1, R6.Pin_0, D3.cathode, D4.anode

notes:
  condicionamento
  condicionamento_ad826

custom parts:
  TL072: Dual Operational Amplifier
  TL072: Dual Operational Amplifier
  TL072: Dual Operational Amplifier
  TL072: Dual Operational Amplifier
