# Fritzing sketch fonte_corrente (saved by Fritzing 0.9.6b)
circuit board: 5cm x 4.5cm
breadboards: 1

parts:
  TL072/AD826 = TL072 [package="DIP (Dual Inline) [THT]"]
  part = TL072 [package="DIP (Dual Inline) [THT]"]
  TL072/AD826_1 = TL072 [package="DIP (Dual Inline) [THT]"]
  TL072/AD826_2 = TL072 [package="DIP (Dual Inline) [THT]"]
  R1 = Resistor [tolerance=±5% resistance=47 power=0.25 package=THT]
  R2 = Resistor [tolerance=±5% resistance=47k power=0.25 package=THT]
  R3 = Resistor [tolerance=±5% resistance=47k power=0.25 package=THT]
  R4 = Resistor [tolerance=±5% resistance=47k power=0.25 package=THT]
  R5 = Resistor [tolerance=±5% resistance=1k power=0.25 package=THT]
  R6 = Resistor [tolerance=±5% resistance=47k power=0.25 package=THT]
  R7 = Resistor [tolerance=±5% resistance=1k power=0.25 package=THT]
  C1 = Electrolytic Capacitor [capacitance=1µF package="100 mil [THT, electrolytic]"]
  C2 = Electrolytic Capacitor [capacitance=1µF package="100 mil [THT, electrolytic]"]
  -V_GND_+V = screw terminal, 3 pins
  gerador_de_sinais = screw terminal, 2 pins
  Saída_de_corrente = screw terminal, 2 pins

nets:
  N1: TL072/AD826.connector0, TL072/AD826.connector1, TL072/AD826_1.pin1, TL072/AD826_1.pin2, R2.Pin_1
  N2: TL072/AD826.connector2, TL072/AD826_1.pin3, R1.Pin_1
  N3: TL072/AD826.connector3, part.pin4, -V_GND_+V.pin3
  N4: TL072/AD826.connector4, TL072/AD826_2.pin5, R4.Pin_0, R6.Pin_0
  N5: TL072/AD826.connector5, TL072/AD826_2.pin6, R2.Pin_0, R3.Pin_1
  N6: TL072/AD826.connector6, TL072/AD826_2.pin7, R3.Pin_0, R5.Pin_0
  N7: TL072/AD826.connector7, part.pin8, -V_GND_+V.pin1
  N8: R1.Pin_0, gerador_de_sinais.pin2
  N9: R4.Pin_1, C1.-, C2.+
  N10: R5.Pin_1, C1.+
  N11: R6.Pin_1, R7.Pin_0
  GND: R7.Pin_1, -V_GND_+V.pin2, gerador_de_sinais.pin1
  N12: C2.-, Saída_de_corrente.pin1, Saída_de_corrente.pin2

notes:
  fonte de corrente

custom parts:
  TL072: Dual Operational Amplifier
  TL072: Dual Operational Amplifier
  TL072: Dual Operational Amplifier
  TL072: Dual Operational Amplifier
