# Fritzing sketch fonte_corrente (saved by Fritzing 0.9.3b)
circuit board: 5cm x 4.5cm
breadboards: 1

parts:
  TL072 = TL072 [package="DIP (Dual Inline) [THT]"]
  Componente1 = TL072 [package="DIP (Dual Inline) [THT]"]
  TL072_1 = TL072 [package="DIP (Dual Inline) [THT]"]
  TL072_2 = TL072 [package="DIP (Dual Inline) [THT]"]
  R1 = Resistor [tolerance=±5% resistance=220 package=THT]
  R2 = Resistor [tolerance=±5% resistance=220 package=THT]
  R3 = Resistor [tolerance=±5% resistance=220 package=THT]
  R4 = Resistor [tolerance=±5% resistance=220 package=THT]
  R5 = Resistor [tolerance=±5% resistance=220 package=THT]
  R6 = Resistor [tolerance=±5% resistance=220 package=THT]
  R7 = Resistor [tolerance=±5% resistance=220 package=THT]
  C1 = Electrolytic Capacitor [capacitance=1µF package="100 mil [THT, electrolytic]"]
  C2 = Electrolytic Capacitor [capacitance=1µF package="100 mil [THT, electrolytic]"]
  signal_In = Screw terminal - 2 pins [package=THT]
  power = screw terminal, 3 pins
  Signal_Out = Screw terminal - 2 pins [package=THT]

nets:
  N1: TL072.connector0, TL072.connector1, TL072_1.pin1, TL072_1.pin2, R2.Pin_1
  N2: TL072.connector2, TL072_1.pin3, R1.Pin_1
  N3: TL072.connector3, Componente1.pin4, power.pin3
  N4: TL072.connector4, TL072_2.pin5, R4.Pin_0, R6.Pin_0
  N5: TL072.connector5, TL072_2.pin6, R3.Pin_1
  N6: TL072.connector6, TL072_2.pin7, R2.Pin_0, R3.Pin_0, R5.Pin_0
  N7: TL072.connector7, Componente1.pin8, power.pin1
  N8: R1.Pin_0, signal_In.pin2
  N9: R4.Pin_1, C1.-, C2.+
  N10: R5.Pin_1, C1.+
  N11: R6.Pin_1, R7.Pin_0
  GND: R7.Pin_1, signal_In.pin1, power.pin2, Signal_Out.pin2
  N12: C2.-, Signal_Out.pin1

notes:
  fonte de corrente

custom parts:
  TL072: Dual Operational Amplifier
  TL072: Dual Operational Amplifier
  TL072: Dual Operational Amplifier
  TL072: Dual Operational Amplifier
