# Fritzing sketch Suporte_para_diversas_saidas (saved by Fritzing 0.9.6b)
circuit board: 9cm x 5cm
breadboards: 1

parts:
  entrada_+V_GND_-V = screw terminal, 3 pins
  +5V_GND = screw terminal, 2 pins
  Saída1_-V_GND_+V = screw terminal, 3 pins
  Saída2_+V_GND_-V = screw terminal, 3 pins
  Saída3_-V_GND_+V = screw terminal, 3 pins
  Saída4_-V_GND_+V = screw terminal, 3 pins
  +V_GND = screw terminal, 2 pins
  C1 = Ceramic Capacitor [capacitance=100nF package="100 mil [THT, multilayer]"]
  C2 = Ceramic Capacitor [capacitance=100nF package="100 mil [THT, multilayer]"]
  7085_out_gnd_in = mystery part, 3 pins [chip_label=?]

nets:
  N1: entrada_+V_GND_-V.pin1, Saída1_-V_GND_+V.pin3, Saída2_+V_GND_-V.pin3, Saída3_-V_GND_+V.pin1, Saída4_-V_GND_+V.pin1, +V_GND.pin2, C2.1, 7085_out_gnd_in.pin3
  N2: entrada_+V_GND_-V.pin2, +5V_GND.pin1, Saída1_-V_GND_+V.pin2, Saída2_+V_GND_-V.pin2, Saída3_-V_GND_+V.pin2, Saída4_-V_GND_+V.pin2, +V_GND.pin1, C1.0, C2.0, 7085_out_gnd_in.pin2
  N3: entrada_+V_GND_-V.pin3, Saída1_-V_GND_+V.pin1, Saída2_+V_GND_-V.pin1, Saída3_-V_GND_+V.pin3, Saída4_-V_GND_+V.pin3
  N4: +5V_GND.pin2, C1.1, 7085_out_gnd_in.pin1
