# Fritzing sketch Suporte_para_diversas_saidas_compacto (saved by Fritzing 0.9.6b)
circuit board: 5.1cm x 5.1cm
breadboards: 1

parts:
  saida1_+V_GND_-V = screw terminal, 3 pins
  saida2_+V_GND_-V = screw terminal, 3 pins
  saida4_+V_GND_-V = screw terminal, 3 pins
  saida5_+V_GND_-V = screw terminal, 3 pins
  Entrada_+V_GND_-V = screw terminal, 3 pins
  saida_gerador_+V_GND_-V = screw terminal, 2 pins
  7085_out_gnd_in = mystery part, 3 pins [chip_label=?]
  C100n = Ceramic Capacitor [capacitance=100nF package="100 mil [THT, multilayer]"]
  C100n_2 = Ceramic Capacitor [capacitance=100nF package="100 mil [THT, multilayer]"]
  saida_stm32_+5V_GND = screw terminal, 2 pins
  saida3_+V_GND_-V = screw terminal, 3 pins

nets:
  N1: saida1_+V_GND_-V.pin1, saida2_+V_GND_-V.pin1, saida4_+V_GND_-V.pin1, saida5_+V_GND_-V.pin1, Entrada_+V_GND_-V.pin1, saida_gerador_+V_GND_-V.pin1, 7085_out_gnd_in.pin3, C100n_2.1, saida3_+V_GND_-V.pin1
  N2: saida1_+V_GND_-V.pin2, saida2_+V_GND_-V.pin2, saida4_+V_GND_-V.pin2, saida5_+V_GND_-V.pin2, Entrada_+V_GND_-V.pin2, saida_gerador_+V_GND_-V.pin2, 7085_out_gnd_in.pin2, C100n.1, C100n_2.0, saida_stm32_+5V_GND.pin1, saida3_+V_GND_-V.pin2
  N3: saida1_+V_GND_-V.pin3, saida2_+V_GND_-V.pin3, saida4_+V_GND_-V.pin3, saida5_+V_GND_-V.pin3, Entrada_+V_GND_-V.pin3, saida3_+V_GND_-V.pin3
  N4: 7085_out_gnd_in.pin1, C100n.0, saida_stm32_+5V_GND.pin2
