# Fritzing sketch fonte_tensao_741 (saved by Fritzing 0.9.3b)
circuit board: 5cm x 5cm
breadboards: 1

parts:
  LM1 = LM741 [part_number=LM741 package="DIP (Dual Inline) [THT]"]
  R1 = Resistor [tolerance=±5% resistance=220k package=THT]
  R2 = Resistor [tolerance=±5% resistance=220k package=THT]
  R3 = Resistor [tolerance=±5% resistance=220k package=THT]
  C1 = Electrolytic Capacitor [capacitance=0.22mF package="100 mil [THT, electrolytic]"]
  Entrada_Fonte_de_tensao_+V = Power Jack [package=power_jack_slot]
  Saída1_+V_GND_-V = screw terminal, 3 pins
  Saída3_+V_GND_-V = screw terminal, 3 pins
  Saída4_+V_GND_-V = screw terminal, 3 pins
  Saída2_+V_GND_-V = screw terminal, 3 pins
  Saída5_+V_GND_-V = screw terminal, 3 pins

nets:
  N1: LM1.pin2, R3.Pin_1, Saída1_+V_GND_-V.pin2, Saída3_+V_GND_-V.pin2, Saída4_+V_GND_-V.pin2, Saída2_+V_GND_-V.pin2, Saída5_+V_GND_-V.pin2
  N2: LM1.pin3, R1.Pin_0, R2.Pin_1
  N3: LM1.pin4, R2.Pin_0, C1.-, Entrada_Fonte_de_tensao_+V.GNDBREAK, Saída1_+V_GND_-V.pin3, Saída3_+V_GND_-V.pin3, Saída4_+V_GND_-V.pin3, Saída2_+V_GND_-V.pin3, Saída5_+V_GND_-V.pin3
  N4: LM1.pin6, R3.Pin_0
  N5: LM1.pin7, R1.Pin_1, C1.+, Entrada_Fonte_de_tensao_+V.PWR, Saída1_+V_GND_-V.pin1, Saída3_+V_GND_-V.pin1, Saída4_+V_GND_-V.pin1, Saída2_+V_GND_-V.pin1, Saída5_+V_GND_-V.pin1

notes:
  fonte de tensão

custom parts:
  LM741: This is a single Op Amp DIP.
