# Fritzing sketch tensao_baseado_lm675 (saved by Fritzing 0.9.3b)
circuit board: 5cm x 4cm
breadboards: 1

parts:
  V_GND = Screw terminal - 2 pins [package=THT]
  +v_gnd_-v = female pin header, 3 pins [form="♀ (female)"]
  R1 = Resistor [tolerance=±5% resistance=22k package=THT]
  R2 = Resistor [tolerance=±5% resistance=22k package=THT]
  R3 = Resistor [tolerance=±5% resistance=1k package=THT]
  R4 = Resistor [tolerance=±5% resistance=15k package=THT]
  lm675 = female pin header, 5 pins [form="♀ (female)"]
  lm676 = female pin header, 5 pins [form="♀ (female)"]
  R5 = Resistor [tolerance=±5% resistance=220 package=THT]
  C1 = Ceramic Capacitor [capacitance=100nF package="100 mil [THT, multilayer]"]

nets:
  GND: V_GND.pin1, +v_gnd_-v.pin3, R2.Pin_1, lm675.pin3, lm676.pin3, C1.0
  N1: V_GND.pin2, +v_gnd_-v.pin1, R1.Pin_0, lm675.pin5, lm676.pin5
  N2: +v_gnd_-v.pin2, R4.Pin_1, lm675.pin4, lm676.pin4, R5.Pin_0
  N3: R1.Pin_1, R2.Pin_0, R3.Pin_0, lm675.pin1, lm676.pin1
  N4: R3.Pin_1, R4.Pin_0, lm675.pin2, lm676.pin2
  N5: R5.Pin_1, C1.1

notes:
  fonte tensao simetrica LM675
  fojnte tensao simetrica lm675
