# Fritzing sketch fonte_tensão (saved by Fritzing 0.9.3b)
circuit board: 5cm x 5cm
breadboards: 1

parts:
  LM1 = LM741 [part_number=LM741 package="DIP (Dual Inline) [THT]"]
  R1 = Resistor [tolerance=±5% resistance=220 package=THT]
  R2 = Resistor [tolerance=±5% resistance=220 package=THT]
  R3 = Resistor [tolerance=±5% resistance=220 package=THT]
  C1 = Electrolytic Capacitor [capacitance=1µF package="100 mil [THT, electrolytic]"]
  power = Power Jack [package=power_jack_slot]
  J7 = screw terminal, 3 pins
  J6 = screw terminal, 3 pins
  J3 = screw terminal, 3 pins
  J4 = screw terminal, 3 pins
  J5 = screw terminal, 3 pins

nets:
  N1: LM1.pin2, R3.Pin_1, J7.pin2, J6.pin2, J3.pin2, J4.pin2, J5.pin2
  N2: LM1.pin3, R1.Pin_0, R2.Pin_1
  N3: LM1.pin4, R2.Pin_0, C1.-, power.GND, J7.pin3, J6.pin3, J3.pin3, J4.pin3, J5.pin3
  N4: LM1.pin6, R3.Pin_0
  N5: LM1.pin7, R1.Pin_1, C1.+, power.PWR, J7.pin1, J6.pin1, J3.pin1, J4.pin1, J5.pin1

notes:
  fonte de tensão

custom parts:
  LM741: This is a single Op Amp DIP.
