# Fritzing sketch gerador_ad9833 (saved by Fritzing 0.9.3b)
circuit board: 9cm x 5cm
breadboards: 1

parts:
  arduino_nano = Arduino Nano (Rev3.0)
  C1 = Ceramic Capacitor [capacitance=100nF package="100 mil [THT, multilayer]"]
  R1 = Resistor [tolerance=±5% resistance=3.3k package=THT]
  TL072 = LM741 [part_number=LM741 package="DIP (Dual Inline) [THT]"]
  1=AGND_2=OUT_3=OUT_filtro_4=OUT_filtro_seguidor = female pin header, 4 pins [form="♀ (female)"]
  borne_saida_filtro_seguidor = screw terminal, 2 pins
  borne_saida_modulo = screw terminal, 2 pins
  1=Vcc_2=DGND_3=SDATA_4=SCLK_5=FSYNC_6=AGND_7=OUT = female pin header, 7 pins [form="♀ (female)"]

nets:
  N1: arduino_nano.GND, 1=Vcc_2=DGND_3=SDATA_4=SCLK_5=FSYNC_6=AGND_7=OUT.pin2
  N2: arduino_nano.D9, 1=Vcc_2=DGND_3=SDATA_4=SCLK_5=FSYNC_6=AGND_7=OUT.pin5
  N3: arduino_nano.D11/MOSI, 1=Vcc_2=DGND_3=SDATA_4=SCLK_5=FSYNC_6=AGND_7=OUT.pin3
  N4: arduino_nano.5V, 1=Vcc_2=DGND_3=SDATA_4=SCLK_5=FSYNC_6=AGND_7=OUT.pin1
  N5: arduino_nano.D13/SCK, 1=Vcc_2=DGND_3=SDATA_4=SCLK_5=FSYNC_6=AGND_7=OUT.pin4
  N6: C1.0, 1=AGND_2=OUT_3=OUT_filtro_4=OUT_filtro_seguidor.pin2, borne_saida_modulo.pin2, 1=Vcc_2=DGND_3=SDATA_4=SCLK_5=FSYNC_6=AGND_7=OUT.pin7
  N7: C1.1, R1.Pin_0, TL072.pin5, 1=AGND_2=OUT_3=OUT_filtro_4=OUT_filtro_seguidor.pin3, borne_saida_filtro_seguidor.pin1
  GND: R1.Pin_1
  N8: TL072.pin6, TL072.pin7
  N9: TL072.pin8, 1=AGND_2=OUT_3=OUT_filtro_4=OUT_filtro_seguidor.pin4, borne_saida_filtro_seguidor.pin2
  N10: 1=AGND_2=OUT_3=OUT_filtro_4=OUT_filtro_seguidor.pin1, borne_saida_modulo.pin1, 1=Vcc_2=DGND_3=SDATA_4=SCLK_5=FSYNC_6=AGND_7=OUT.pin6

notes:
  gerador moduload9833

custom parts:
  LM741: This is a single Op Amp DIP.
