# Fritzing sketch gerador_ad9833_versao_2 (saved by Fritzing 0.9.3b)
circuit board: 10cm x 10cm
breadboards: 1

parts:
  arduino_nano = Arduino Nano (Rev3.0)
  GND_5V = female pin header, 2 pins [form="♀ (female)"]
  TL72_1 = LM741 [part_number=LM741 package="DIP (Dual Inline) [THT]"]
  1=Vcc_2=DGND_3=SDATA_4=SCLK_5=FSYNC_6=AGND_7=OUT = female pin header, 7 pins [form="♀ (female)"]
  1=AGND_2=OUT_MOD = female pin header, 2 pins [form="♀ (female)"]
  C1 = Ceramic Capacitor [capacitance=100nF package="100 mil [THT, multilayer]"]
  R1 = Resistor [tolerance=±5% resistance=680k package=THT]
  1=GND_2=SAIDA_SEGUIDOR1 = female pin header, 2 pins [form="♀ (female)"]
  1=AGND_2=OUT_MOD1 = female pin header, 2 pins [form="♀ (female)"]
  1=GND_2=SAIDA_SEGUIDOR1_2 = female pin header, 2 pins [form="♀ (female)"]
  1=GND_2_=SAIDA_PASSA_ALTA = female pin header, 2 pins [form="♀ (female)"]
  1=GND_2_=SAIDA_PASSA_ALTA1 = female pin header, 2 pins [form="♀ (female)"]
  TL72_2 = LM741 [part_number=LM741 package="DIP (Dual Inline) [THT]"]
  1=GND_2=SAIDA_SEGUIDOR2 = female pin header, 2 pins [form="♀ (female)"]
  1=GND_2=SAIDA_SEGUIDOR2_2 = female pin header, 2 pins [form="♀ (female)"]
  TL72_3 = LM741 [part_number=LM741 package="DIP (Dual Inline) [THT]"]
  R2 = TRIMPOT [package=3386u]
  R3 = Resistor [tolerance=±5% resistance=1k package=THT]
  1=GND_2_=saidaGanho = female pin header, 2 pins [form="♀ (female)"]
  1=I2C_CLK_2=I2C_DATA_3=SPI_SCK_4=SPI_MISO_5=SPI_MOSI_6=SPI_SS_7=UART_IN_8=UART_OUT = female pin header, 8 pins [form="♀ (female)"]
  1=gnd_2=3_3v_3=5v = female pin header, 3 pins [form="♀ (female)"]
  1=gnd_2=saida_modulo_3=saida_seguidor1_4=saida_filtro_PA_5=saida_seguidor2_6=saida_ganho = female pin header, 6 pins [form="♀ (female)"]

nets:
  N1: arduino_nano.D1/TX, 1=I2C_CLK_2=I2C_DATA_3=SPI_SCK_4=SPI_MISO_5=SPI_MOSI_6=SPI_SS_7=UART_IN_8=UART_OUT.pin8
  N2: arduino_nano.D0/RX, 1=I2C_CLK_2=I2C_DATA_3=SPI_SCK_4=SPI_MISO_5=SPI_MOSI_6=SPI_SS_7=UART_IN_8=UART_OUT.pin7
  GND: arduino_nano.GND, GND_5V.pin1, 1=Vcc_2=DGND_3=SDATA_4=SCLK_5=FSYNC_6=AGND_7=OUT.pin2, 1=Vcc_2=DGND_3=SDATA_4=SCLK_5=FSYNC_6=AGND_7=OUT.pin6, 1=AGND_2=OUT_MOD.pin1, 1=gnd_2=3_3v_3=5v.pin1, 1=gnd_2=saida_modulo_3=saida_seguidor1_4=saida_filtro_PA_5=saida_seguidor2_6=saida_ganho.pin1, 1=gnd_2=saida_modulo_3=saida_seguidor1_4=saida_filtro_PA_5=saida_seguidor2_6=saida_ganho.pin2
  N3: arduino_nano.D9, 1=Vcc_2=DGND_3=SDATA_4=SCLK_5=FSYNC_6=AGND_7=OUT.pin5
  N4: arduino_nano.D10, 1=I2C_CLK_2=I2C_DATA_3=SPI_SCK_4=SPI_MISO_5=SPI_MOSI_6=SPI_SS_7=UART_IN_8=UART_OUT.pin6
  N5: arduino_nano.D11/MOSI, 1=Vcc_2=DGND_3=SDATA_4=SCLK_5=FSYNC_6=AGND_7=OUT.pin3, 1=I2C_CLK_2=I2C_DATA_3=SPI_SCK_4=SPI_MISO_5=SPI_MOSI_6=SPI_SS_7=UART_IN_8=UART_OUT.pin5
  N6: arduino_nano.D12/MISO, 1=I2C_CLK_2=I2C_DATA_3=SPI_SCK_4=SPI_MISO_5=SPI_MOSI_6=SPI_SS_7=UART_IN_8=UART_OUT.pin4
  N7: arduino_nano.5V, GND_5V.pin2, 1=Vcc_2=DGND_3=SDATA_4=SCLK_5=FSYNC_6=AGND_7=OUT.pin1, 1=gnd_2=3_3v_3=5v.pin3
  N8: arduino_nano.A5, 1=I2C_CLK_2=I2C_DATA_3=SPI_SCK_4=SPI_MISO_5=SPI_MOSI_6=SPI_SS_7=UART_IN_8=UART_OUT.pin1
  N9: arduino_nano.A4, 1=I2C_CLK_2=I2C_DATA_3=SPI_SCK_4=SPI_MISO_5=SPI_MOSI_6=SPI_SS_7=UART_IN_8=UART_OUT.pin2
  N10: arduino_nano.3V3, 1=gnd_2=3_3v_3=5v.pin2
  N11: arduino_nano.D13/SCK, 1=Vcc_2=DGND_3=SDATA_4=SCLK_5=FSYNC_6=AGND_7=OUT.pin4, 1=I2C_CLK_2=I2C_DATA_3=SPI_SCK_4=SPI_MISO_5=SPI_MOSI_6=SPI_SS_7=UART_IN_8=UART_OUT.pin3
  N12: TL72_1.pin1, TL72_1.pin2, 1=GND_2=SAIDA_SEGUIDOR1.pin2, 1=gnd_2=saida_modulo_3=saida_seguidor1_4=saida_filtro_PA_5=saida_seguidor2_6=saida_ganho.pin3
  N13: TL72_1.pin3, 1=AGND_2=OUT_MOD1.pin2
  N14: 1=Vcc_2=DGND_3=SDATA_4=SCLK_5=FSYNC_6=AGND_7=OUT.pin7, 1=AGND_2=OUT_MOD.pin2
  N15: C1.0, R1.Pin_0, 1=GND_2_=SAIDA_PASSA_ALTA.pin2, 1=gnd_2=saida_modulo_3=saida_seguidor1_4=saida_filtro_PA_5=saida_seguidor2_6=saida_ganho.pin4
  N16: C1.1, 1=GND_2=SAIDA_SEGUIDOR1_2.pin2
  N17: R1.Pin_1, 1=GND_2=SAIDA_SEGUIDOR1_2.pin1, 1=GND_2_=SAIDA_PASSA_ALTA.pin1
  N18: 1=GND_2=SAIDA_SEGUIDOR1.pin1, 1=AGND_2=OUT_MOD1.pin1
  N19: 1=GND_2_=SAIDA_PASSA_ALTA1.pin1, 1=GND_2=SAIDA_SEGUIDOR2.pin1
  N20: 1=GND_2_=SAIDA_PASSA_ALTA1.pin2, TL72_2.pin3
  N21: TL72_2.pin1, TL72_2.pin2, 1=GND_2=SAIDA_SEGUIDOR2.pin2, 1=gnd_2=saida_modulo_3=saida_seguidor1_4=saida_filtro_PA_5=saida_seguidor2_6=saida_ganho.pin5
  N22: 1=GND_2=SAIDA_SEGUIDOR2_2.pin1, R3.Pin_1, 1=GND_2_=saidaGanho.pin1
  N23: 1=GND_2=SAIDA_SEGUIDOR2_2.pin2, TL72_3.pin3
  N24: TL72_3.pin1, R2.CW, 1=GND_2_=saidaGanho.pin2, 1=gnd_2=saida_modulo_3=saida_seguidor1_4=saida_filtro_PA_5=saida_seguidor2_6=saida_ganho.pin6
  N25: TL72_3.pin2, R2.CCW, R2.WIPER, R3.Pin_0

custom parts:
  LM741: This is a single Op Amp DIP.
