# Fritzing sketch ResistorSentinela (saved by Fritzing 0.9.3b)
circuit board: 4cm x 3cm
breadboards: 1

parts:
  ina128 = LM741 [package="DIP (Dual Inline) [THT]"]
  Rsentinela = Resistor [tolerance=±5% resistance=47 package=THT]
  signal_Out = screw terminal, 2 pins
  RganhoINA = Resistor [tolerance=±5% resistance=1.5k package=THT]
  Alimentação_-V_GND_+V = screw terminal, 3 pins
  Signal_In = screw terminal, 2 pins

nets:
  N1: ina128.pin1, RganhoINA.Pin_0
  N2: ina128.pin2, Rsentinela.Pin_1, Signal_In.pin2
  GND: ina128.pin3, ina128.pin5, Rsentinela.Pin_0, Alimentação_-V_GND_+V.pin2, Signal_In.pin1
  N3: ina128.pin4, Alimentação_-V_GND_+V.pin3
  N4: ina128.pin6, signal_Out.pin1, signal_Out.pin2
  N5: ina128.pin7, Alimentação_-V_GND_+V.pin1
  N6: ina128.pin8, RganhoINA.Pin_1

notes:
  sentinela

custom parts:
  LM741: This is a single Op Amp DIP.
