# Fritzing sketch SMT32 (saved by Fritzing 0.9.3b)
circuit board: 8.46667cm x 5.64444cm
breadboards: 1

parts:
  i2c = female pin header, 2 pins [form="♀ (female)"]  # not connected
  i2c1 = female pin header, 2 pins [form="♀ (female)"]  # not connected
  SPI = female pin header, 4 pins [form="♀ (female)"]  # not connected
  SPI1 = female pin header, 4 pins [form="♀ (female)"]
  SPI2 = female pin header, 4 pins [form="♀ (female)"]
  stm32-1 = female pin header, 20 pins [form="♀ (female)"]
  J4 = female pin header, 20 pins [form="♀ (female)"]
  stm32-2 = female pin header, 20 pins [form="♀ (female)"]
  J3 = female pin header, 20 pins [form="♀ (female)"]
  +5v_gnd_+3_3v = female pin header, 3 pins [form="♀ (female)"]
  gnd_+3_3v = female pin header, 2 pins [form="♀ (female)"]

nets:
  N1: SPI1.pin1, stm32-2.pin17, J3.pin17
  N2: SPI1.pin2, stm32-2.pin18, J3.pin18
  N3: SPI1.pin3, stm32-2.pin19, J3.pin19
  N4: SPI1.pin4, stm32-2.pin20, J3.pin20
  N5: SPI2.pin1, stm32-1.pin9, J4.pin9
  N6: SPI2.pin2, stm32-1.pin10, J4.pin10
  N7: SPI2.pin3, stm32-1.pin11, J4.pin11
  N8: SPI2.pin4, stm32-1.pin12, J4.pin12
  N9: stm32-1.pin1, J4.pin1
  N10: stm32-1.pin2, J4.pin2
  N11: stm32-1.pin3, J4.pin3
  N12: stm32-1.pin4, J4.pin4
  N13: stm32-1.pin5, J4.pin5
  N14: stm32-1.pin6, J4.pin6
  N15: stm32-1.pin7, J4.pin7
  N16: stm32-1.pin8, J4.pin8
  N17: stm32-1.pin13, J4.pin13
  N18: stm32-1.pin14, J4.pin14
  N19: stm32-1.pin15, J4.pin15
  N20: stm32-1.pin16, J4.pin16
  N21: stm32-1.pin17, J4.pin17
  N22: stm32-1.pin18, J4.pin18, gnd_+3_3v.pin1
  N23: stm32-1.pin19, J4.pin19, gnd_+3_3v.pin2
  N24: stm32-1.pin20, J4.pin20
  N25: stm32-2.pin1, J3.pin1, +5v_gnd_+3_3v.pin1
  N26: stm32-2.pin2, J3.pin2, +5v_gnd_+3_3v.pin2
  N27: stm32-2.pin3, J3.pin3, +5v_gnd_+3_3v.pin3
  N28: stm32-2.pin4, J3.pin4
  N29: stm32-2.pin5, J3.pin5
  N30: stm32-2.pin6, J3.pin6
  N31: stm32-2.pin7, J3.pin7
  N32: stm32-2.pin8, J3.pin8
  N33: stm32-2.pin9, J3.pin9
  N34: stm32-2.pin10, J3.pin10
  N35: stm32-2.pin11, J3.pin11
  N36: stm32-2.pin12, J3.pin12
  N37: stm32-2.pin13, J3.pin13
  N38: stm32-2.pin14, J3.pin14
  N39: stm32-2.pin15, J3.pin15
  N40: stm32-2.pin16, J3.pin16
