# Fritzing sketch SMT32 (saved by Fritzing 0.9.3b)
circuit board: 5cm x 6cm
breadboards: 1

parts:
  stm32-1 = female pin header, 20 pins [form="♀ (female)"]
  J4 = female pin header, 20 pins [form="♀ (female)"]
  stm32-2 = female pin header, 20 pins [form="♀ (female)"]
  J3 = female pin header, 20 pins [form="♀ (female)"]
  J5 = female pin header, 20 pins [form="♀ (female)"]
  J6 = female pin header, 20 pins [form="♀ (female)"]
  J7 = female pin header, 20 pins [form="♀ (female)"]
  J8 = female pin header, 20 pins [form="♀ (female)"]

nets:
  N1: stm32-1.pin1, J4.pin1, J5.pin1, J6.pin1
  N2: stm32-1.pin2, J4.pin2, J5.pin2, J6.pin2
  N3: stm32-1.pin3, J4.pin3, J5.pin3, J6.pin3
  N4: stm32-1.pin4, J4.pin4, J5.pin4, J6.pin4
  N5: stm32-1.pin5, J4.pin5, J5.pin5, J6.pin5
  N6: stm32-1.pin6, J4.pin6, J5.pin6, J6.pin6
  N7: stm32-1.pin7, J4.pin7, J5.pin7, J6.pin7
  N8: stm32-1.pin8, J4.pin8, J5.pin8, J6.pin8
  N9: stm32-1.pin9, J4.pin9, J5.pin9, J6.pin9
  N10: stm32-1.pin10, J4.pin10, J5.pin10, J6.pin10
  N11: stm32-1.pin11, J4.pin11, J5.pin11, J6.pin11
  N12: stm32-1.pin12, J4.pin12, J5.pin12, J6.pin12
  N13: stm32-1.pin13, J4.pin13, J5.pin13, J6.pin13
  N14: stm32-1.pin14, J4.pin14, J5.pin14, J6.pin14
  N15: stm32-1.pin15, J4.pin15, J5.pin15, J6.pin15
  N16: stm32-1.pin16, J4.pin16, J5.pin16, J6.pin16
  N17: stm32-1.pin17, J4.pin17, J5.pin17, J6.pin17
  N18: stm32-1.pin18, J4.pin18, J5.pin18, J6.pin18
  N19: stm32-1.pin19, J4.pin19, J5.pin19, J6.pin19
  N20: stm32-1.pin20, J4.pin20, J5.pin20, J6.pin20
  N21: stm32-2.pin1, J3.pin1, J7.pin1, J8.pin1
  N22: stm32-2.pin2, J3.pin2, J7.pin2, J8.pin2
  N23: stm32-2.pin3, J3.pin3, J7.pin3, J8.pin3
  N24: stm32-2.pin4, J3.pin4, J7.pin4, J8.pin4
  N25: stm32-2.pin5, J3.pin5, J7.pin5, J8.pin5
  N26: stm32-2.pin6, J3.pin6, J7.pin6, J8.pin6
  N27: stm32-2.pin7, J3.pin7, J7.pin7, J8.pin7
  N28: stm32-2.pin8, J3.pin8, J7.pin8, J8.pin8
  N29: stm32-2.pin9, J3.pin9, J7.pin9, J8.pin9
  N30: stm32-2.pin10, J3.pin10, J7.pin10, J8.pin10
  N31: stm32-2.pin11, J3.pin11, J7.pin11, J8.pin11
  N32: stm32-2.pin12, J3.pin12, J7.pin12, J8.pin12
  N33: stm32-2.pin13, J3.pin13, J7.pin13, J8.pin13
  N34: stm32-2.pin14, J3.pin14, J7.pin14, J8.pin14
  N35: stm32-2.pin15, J3.pin15, J7.pin15, J8.pin15
  N36: stm32-2.pin16, J3.pin16, J7.pin16, J8.pin16
  N37: stm32-2.pin17, J3.pin17, J7.pin17, J8.pin17
  N38: stm32-2.pin18, J3.pin18, J7.pin18, J8.pin18
  N39: stm32-2.pin19, J3.pin19, J7.pin19, J8.pin19
  N40: stm32-2.pin20, J3.pin20, J7.pin20, J8.pin20

notes:
  smtm32 bluepill
