# Fritzing sketch gerador_ad9833_sem_ganho (saved by Fritzing 0.9.6b)
circuit board: 10cm x 5cm
breadboards: 1

parts:
  arduino_nano = Arduino Nano (Rev3.0)
  C1 = Ceramic Capacitor [capacitance=100nF package="100 mil [THT, multilayer]"]
  R1 = Resistor [tolerance=±5% resistance=3.3k power=0.25 package=THT]
  TL072/AD826 = LM741 [part_number=LM741 package="DIP (Dual Inline) [THT]"]
  1=AGND_2=OUT_3=OUT_filtro_4=OUT_filtro_seguidor = female pin header, 4 pins [form="♀ (female)"]
  1=Vcc_2=DGND_3=SDATA_4=SCLK_5=FSYNC_6=AGND_7=OUT = female pin header, 7 pins [form="♀ (female)"]
  GND_5V = female pin header, 2 pins [form="♀ (female)"]
  -V_+V = female pin header, 2 pins [form="♀ (female)"]

nets:
  GND: arduino_nano.GND, R1.Pin_1, 1=AGND_2=OUT_3=OUT_filtro_4=OUT_filtro_seguidor.pin1, 1=Vcc_2=DGND_3=SDATA_4=SCLK_5=FSYNC_6=AGND_7=OUT.pin2, 1=Vcc_2=DGND_3=SDATA_4=SCLK_5=FSYNC_6=AGND_7=OUT.pin6, GND_5V.pin1
  N1: arduino_nano.D9, 1=Vcc_2=DGND_3=SDATA_4=SCLK_5=FSYNC_6=AGND_7=OUT.pin5
  N2: arduino_nano.D11/MOSI, 1=Vcc_2=DGND_3=SDATA_4=SCLK_5=FSYNC_6=AGND_7=OUT.pin3
  N3: arduino_nano.5V, 1=Vcc_2=DGND_3=SDATA_4=SCLK_5=FSYNC_6=AGND_7=OUT.pin1, GND_5V.pin2
  N4: arduino_nano.D13/SCK, 1=Vcc_2=DGND_3=SDATA_4=SCLK_5=FSYNC_6=AGND_7=OUT.pin4
  N5: C1.0, TL072/AD826.pin1, TL072/AD826.pin2
  N6: C1.1, R1.Pin_0, TL072/AD826.pin5, 1=AGND_2=OUT_3=OUT_filtro_4=OUT_filtro_seguidor.pin3
  N7: TL072/AD826.pin3, 1=AGND_2=OUT_3=OUT_filtro_4=OUT_filtro_seguidor.pin2, 1=Vcc_2=DGND_3=SDATA_4=SCLK_5=FSYNC_6=AGND_7=OUT.pin7
  N8: TL072/AD826.pin4, -V_+V.pin2
  N9: TL072/AD826.pin6, TL072/AD826.pin7, 1=AGND_2=OUT_3=OUT_filtro_4=OUT_filtro_seguidor.pin4
  N10: TL072/AD826.pin8, -V_+V.pin1

notes:
  gerador moduloAD9833
  gerador funcoes moduloAD9833

custom parts:
  LM741: This is a single Op Amp DIP.
