# Fritzing sketch resistor_sentinela (saved by Fritzing 0.9.3b)
breadboards: 1

parts:
  U1 = mystery part, 8 pins [chip_label=?]
  Rg = Resistor [tolerance=±5% resistance=220 package=THT]
  Vin = screw terminal, 2 pins
  out = screw terminal, 2 pins
  -V_GND_+V = screw terminal, 3 pins
  R1 = Resistor [tolerance=±5% resistance=220 package=THT]
  R2 = Resistor [tolerance=±5% resistance=220 package=THT]
  R3 = Resistor [tolerance=±5% resistance=220 package=THT]
  R4 = Resistor [tolerance=±5% resistance=220 package=THT]
  C1 = Ceramic Capacitor [capacitance=100nF package="100 mil [THT, multilayer]"]
  C2 = Ceramic Capacitor [capacitance=100nF package="100 mil [THT, multilayer]"]
  Vin-acoplamentoAC = screw terminal, 2 pins
  sentinela = Resistor [tolerance=±5% resistance=220 package=THT]

nets:
  N1: U1.pin1, Rg.Pin_0
  N2: U1.pin2, Vin.pin2, R2.Pin_1, C1.0, sentinela.Pin_0
  N3: U1.pin3, Vin.pin1, R4.Pin_0, C2.0, sentinela.Pin_1
  N4: U1.pin4, -V_GND_+V.pin3
  N5: U1.pin5, -V_GND_+V.pin2
  N6: U1.pin6, out.pin1, out.pin2
  N7: U1.pin7, -V_GND_+V.pin1
  N8: U1.pin8, Rg.Pin_1
  N9: R1.Pin_0, R2.Pin_0, R3.Pin_1, R4.Pin_1
  N10: R1.Pin_1, C1.1, Vin-acoplamentoAC.pin2
  N11: R3.Pin_0, C2.1, Vin-acoplamentoAC.pin1
